// Logisim project CPU.circ as structural Verilog: 3 circuits, main circuit main
module main (
);

  Timer timer_1 ();  // open: Increment, Clock, Clear, T0, T1, T2, T3, T4, T5, T6, T7, T8, T9, T10, T11, T12, T13, T14, T15, Overflow
endmodule

module Timer (
  input  Increment,
  input  Clock,
  input  Clear,
  output T0,
  output T1,
  output T2,
  output T3,
  output T4,
  output T5,
  output T6,
  output T7,
  output T8,
  output T9,
  output T10,
  output T11,
  output T12,
  output T13,
  output T14,
  output T15,
  output Overflow
);

  wire [3:0] counter_1_q;

  Counter #(.width(4), .max('hf)) counter_1 (
    .count(Increment), .Q(counter_1_q), .carry(Overflow), .clk(Clock), .clr(Clear));  // open: load, D
  Decoder #(.select(4)) decoder_1 (
    .out0(T0), .out1(T1), .out2(T2), .out3(T3), .out4(T4), .out5(T5), .out6(T6), .out7(T7), .out8(T8),
    .out9(T9), .out10(T10), .out11(T11), .out12(T12), .out13(T13), .out14(T14), .out15(T15), .sel(counter_1_q));  // open: en
endmodule

module _16b_register (
  input  in_1,
  input  in_2,
  input  in_3,
  input  in_4,
  input  in_5,
  input  in_6,
  input  in_7,
  input  in_8,
  input  in_9,
  input  in_10,
  input  in_11,
  input  in_12,
  input  in_13,
  output out_14,
  output out_15,
  output out_16,
  output out_17,
  output out_18,
  output out_19,
  output out_20,
  output out_21,
  output out_22,
  output out_23,
  output out_24,
  output out_25
);

  D_Flip_Flop d_ff_1 (.clk(in_1), .D(in_2), .Q(out_14));  // open: Qn, preset, en, reset
  D_Flip_Flop d_ff_2 (.clk(in_1), .D(in_3), .Q(out_15));  // open: Qn, preset, en, reset
  D_Flip_Flop d_ff_3 (.clk(in_1), .D(in_4), .Q(out_16));  // open: Qn, preset, en, reset
  D_Flip_Flop d_ff_4 (.clk(in_1), .D(in_5), .Q(out_17));  // open: Qn, preset, en, reset
  D_Flip_Flop d_ff_5 (.clk(in_1), .D(in_6), .Q(out_18));  // open: Qn, preset, en, reset
  D_Flip_Flop d_ff_6 (.clk(in_1), .D(in_7), .Q(out_19));  // open: Qn, preset, en, reset
  D_Flip_Flop d_ff_7 (.clk(in_1), .D(in_8), .Q(out_20));  // open: Qn, preset, en, reset
  D_Flip_Flop d_ff_8 (.clk(in_1), .D(in_9), .Q(out_21));  // open: Qn, preset, en, reset
  D_Flip_Flop d_ff_9 (.clk(in_1), .D(in_10), .Q(out_22));  // open: Qn, preset, en, reset
  D_Flip_Flop d_ff_10 (.clk(in_1), .D(in_11), .Q(out_23));  // open: Qn, preset, en, reset
  D_Flip_Flop d_ff_11 (.clk(in_1), .D(in_12), .Q(out_24));  // open: Qn, preset, en, reset
  D_Flip_Flop d_ff_12 (.clk(in_1), .D(in_13), .Q(out_25));  // open: Qn, preset, en, reset
endmodule
